// Logisim project ALU.circ as structural Verilog: 1 circuit, main circuit ALU
module ALU (
  input  [2:0] Op,
  input  [31:0] in_2,
  input  [31:0] in_3,
  output out_4,
  output [31:0] Result
);

  wire [31:0] A_B, A_B_t, A_B_t_t, A_B_t_t_t;

  assign A_B = in_2 & in_3;  // AND_Gate and_1, 32 bits wide
  assign A_B_t_t_t = in_2 | in_3;  // OR_Gate or_1, 32 bits wide
  Adder #(.width(32)) adder_1 (.a(in_2), .b(in_3), .out(A_B_t));  // open: cin, cout
  Subtractor #(.width(32)) subtractor_1 (.a(in_2), .b(in_3), .out(A_B_t_t));  // open: bin, bout
  Comparator #(.width(32), .mode("unsigned")) comparator_1 (.a(in_2), .b(in_3), .eq(out_4));  // open: gt, lt
  Multiplexer #(.select(3), .width(32)) multiplexer_1 (
    .in0(A_B_t), .in1(A_B_t_t), .in2(A_B_t_t_t), .in3(A_B), .out(Result), .sel(Op));  // open: in4, in5, in6, in7, en

  // Other names for the same wires on the sheet: A[31:0] = in_2; B[31:0] = in_3; Zero = out_4
endmodule
