// Logisim project Control Unit.circ as structural Verilog: 1 circuit, main circuit Control Unit
// Control
module Control_Unit (
  input  [5:0] opcode,
  input  [5:0] func,
  output [2:0] out_3,
  output out_4,
  output out_5,
  output out_6,
  output [1:0] out_7,
  output out_8,
  output out_9,
  output out_10
);

  wire addu_func_out, addu_out, beq_out, lui_out, lw_out, not_1_out, not_2_out, not_3_out, not_4_out,
       not_5_out, not_6_out, not_7_out, not_8_out, not_9_out, not_10_out, not_11_out, not_12_out, ori_out,
       special_out, subu_func_out, subu_out, sw_out;

  not not_1 (not_1_out, opcode[5]);
  not not_2 (not_2_out, opcode[4]);
  not not_3 (not_3_out, opcode[3]);
  not not_4 (not_4_out, opcode[2]);
  not not_5 (not_5_out, opcode[1]);
  not not_6 (not_6_out, opcode[0]);
  not not_7 (not_7_out, func[4]);
  not not_8 (not_8_out, func[5]);
  not not_9 (not_9_out, func[3]);
  not not_10 (not_10_out, func[2]);
  not not_11 (not_11_out, func[1]);
  not not_12 (not_12_out, func[0]);
  and addu_func (addu_func_out, func[0], not_11_out, not_10_out, not_9_out, not_7_out, func[5]);
  and special (special_out, not_6_out, not_5_out, not_4_out, not_3_out, not_2_out, not_1_out);
  and subu_func (subu_func_out, func[0], func[1], not_10_out, not_9_out, not_7_out, func[5]);
  and addu (addu_out, addu_func_out, special_out);
  and subu (subu_out, special_out, subu_func_out);
  and ori (ori_out, opcode[0], not_5_out, opcode[2], opcode[3], not_2_out, not_1_out);
  and lw (lw_out, opcode[0], opcode[1], not_4_out, not_3_out, not_2_out, opcode[5]);
  and sw (sw_out, opcode[0], opcode[1], not_4_out, opcode[3], not_2_out, opcode[5]);
  and beq (beq_out, not_6_out, not_5_out, opcode[2], not_3_out, not_2_out, not_1_out);
  and lui (lui_out, opcode[0], opcode[1], opcode[2], opcode[3], not_2_out, not_1_out);
  or ALUOp2 (out_3[2], 1'b0, 1'b0);
  or ALUOp1 (out_3[1], 1'b0, ori_out);
  or ALUOp0 (out_3[0], 1'b0, subu_out);
  or ALUSrc (out_4, lw_out, sw_out, ori_out);
  or RegWrite (out_5, addu_out, subu_out, lw_out, lui_out, ori_out);
  or MemtoReg (out_6, lw_out, 1'b0);
  or ExtOp1 (out_7[1], 1'b0, lui_out);
  or ExtOp0 (out_7[0], 1'b0, ori_out);
  or RegDst (out_8, subu_out, addu_out);
  or NPCOp (out_9, 1'b0, beq_out);
  or MemWrite (out_10, 1'b0, sw_out);

  // Other names for the same wires on the sheet: ALUOp[2:0] = out_3; ALUSrc = out_4; EXTOp[1:0] = out_7;
  //   MemtoReg = out_6; MemWrite = out_10; NPCOp = out_9; op0 = opcode[0]; op1 = opcode[1]; op2 = opcode[2];
  //   op3 = opcode[3]; op4 = opcode[4]; op5 = opcode[5]; RegDst = out_8; RegWrite = out_5
endmodule
