// Logisim project DIS.circ as structural Verilog: 1 circuit, main circuit distribute
// dis
module distribute (
  input  [31:0] in_1,
  output [5:0] out_2,
  output [5:0] out_3,
  output [4:0] out_4,
  output [4:0] out_5,
  output [4:0] out_6,
  output [15:0] out_7,
  output [4:0] out_8,
  output [25:0] out_9
);


  assign out_2 = in_1[31:26];
  assign out_3 = in_1[5:0];
  assign out_4 = in_1[15:11];
  assign out_5 = in_1[20:16];
  assign out_6 = in_1[25:21];
  assign out_7 = in_1[15:0];
  assign out_8 = in_1[10:6];
  assign out_9 = in_1[25:0];

  // Other names for the same wires on the sheet: address[25:0] = in_1[25:0]; func[5:0] = in_1[5:0];
  //   immediate[15:0] = in_1[15:0]; Opcode[5:0] = in_1[31:26]; rd[4:0] = in_1[15:11]; rs[4:0] = in_1[25:21];
  //   rt[4:0] = in_1[20:16]; shamt[4:0] = in_1[10:6]
endmodule
