// Logisim project DM.circ as structural Verilog: 1 circuit, main circuit DM
module DM (
  input  in_1,
  input  [31:0] Address,
  input  [31:0] WriteData,
  input  clk,
  input  reset,
  output [31:0] ReadData
);

  RAM #(.addrWidth(5), .dataWidth(32), .bus("separate")) ram_1 (
    .addr(Address[6:2]), .din(WriteData), .data(ReadData), .str(in_1), .clk(clk), .clr(reset));  // open: sel, ld

  // Other names for the same wires on the sheet: MemWrite = in_1
endmodule
