// Logisim project EXT.circ as structural Verilog: 1 circuit, main circuit EXT
module EXT (
  input  [1:0] EXTOp,
  input  [15:0] imme,
  output [31:0] out_3
);

  wire [31:0] bit_extender_1_out, bit_extender_2_out, bit_extender_3_out, shifter_1_out;

  assign bit_extender_1_out = {{16{imme[15]}}, imme};  // Bit_Extender bit_extender_1
  assign bit_extender_2_out = {{16{1'b0}}, imme};  // Bit_Extender bit_extender_2
  assign bit_extender_3_out = {{16{1'b0}}, imme};  // Bit_Extender bit_extender_3
  Shifter #(.width(32)) shifter_1 (.in(bit_extender_3_out), .\dist (5'b10000), .out(shifter_1_out));
  Multiplexer #(.select(2), .width(32)) multiplexer_1 (
    .in0(bit_extender_1_out), .in1(bit_extender_2_out), .in2(shifter_1_out), .out(out_3), .sel(EXTOp));  // open: in3, en
endmodule
