// Logisim project GRF.circ as structural Verilog: 1 circuit, main circuit grf
// GRF
module grf (
  input  clk,
  input  reset,
  input  WE,
  input  [4:0] A1,
  input  [4:0] A2,
  input  [4:0] A3,
  input  [31:0] WD,
  output [31:0] RD1,
  output [31:0] RD2
);

  wire WE0, WE1, WE2, WE3, WE4, WE5, WE6, WE7, WE8, WE9, WE10, WE11, WE12, WE13, WE14, WE15, WE16, WE17,
       WE18, WE19, WE20, WE21, WE22, WE23, WE24, WE25, WE26, WE27, WE28, WE29, WE30, WE31;
  wire [31:0] R0, R1, R1D, R2, R2D, R3, R3D, R4, R4D, R5, R5D, R6, R6D, R7, R7D, R8, R8D, R9, R9D, R10, R10D,
       R11, R11D, R12, R12D, R13, R13D, R14, R14D, R15, R15D, R16, R16D, R17, R17D, R18, R18D, R19, R19D,
       R20, R20D, R21, R21D, R22, R22D, R23, R23D, R24, R24D, R25, R25D, R26, R26D, R27, R27D, R28, R28D,
       R29, R29D, R30, R30D, R31, R31D;

  Demultiplexer #(.select(5), .width(32)) demultiplexer_1 (
    .out1(R1D), .out2(R2D), .out3(R3D), .out4(R4D), .out5(R5D), .out6(R6D), .out7(R7D), .out8(R8D),
    .out9(R9D), .out10(R10D), .out11(R11D), .out12(R12D), .out13(R13D), .out14(R14D), .out15(R15D),
    .out16(R16D), .out17(R17D), .out18(R18D), .out19(R19D), .out20(R20D), .out21(R21D), .out22(R22D),
    .out23(R23D), .out24(R24D), .out25(R25D), .out26(R26D), .out27(R27D), .out28(R28D), .out29(R29D),
    .out30(R30D), .out31(R31D), .in(WD), .sel(A3));  // open: out0, en
  Register #(.width(32)) register_1 (.en(WE0), .Q(R0), .clk(clk), .clr(reset));  // open: D
  Register #(.width(32)) register_2 (.D(R8D), .en(WE8), .Q(R8), .clk(clk), .clr(reset));
  Register #(.width(32)) register_3 (.D(R16D), .en(WE16), .Q(R16), .clk(clk), .clr(reset));
  Register #(.width(32)) register_4 (.D(R24D), .en(WE24), .Q(R24), .clk(clk), .clr(reset));
  Register #(.width(32)) register_5 (.D(R1D), .en(WE1), .Q(R1), .clk(clk), .clr(reset));
  Register #(.width(32)) register_6 (.D(R9D), .en(WE9), .Q(R9), .clk(clk), .clr(reset));
  Register #(.width(32)) register_7 (.D(R17D), .en(WE17), .Q(R17), .clk(clk), .clr(reset));
  Register #(.width(32)) register_8 (.D(R25D), .en(WE25), .Q(R25), .clk(clk), .clr(reset));
  Demultiplexer #(.select(5)) demultiplexer_2 (
    .out0(WE0), .out1(WE1), .out2(WE2), .out3(WE3), .out4(WE4), .out5(WE5), .out6(WE6), .out7(WE7),
    .out8(WE8), .out9(WE9), .out10(WE10), .out11(WE11), .out12(WE12), .out13(WE13), .out14(WE14),
    .out15(WE15), .out16(WE16), .out17(WE17), .out18(WE18), .out19(WE19), .out20(WE20), .out21(WE21),
    .out22(WE22), .out23(WE23), .out24(WE24), .out25(WE25), .out26(WE26), .out27(WE27), .out28(WE28),
    .out29(WE29), .out30(WE30), .out31(WE31), .in(WE), .sel(A3));  // open: en
  Register #(.width(32)) register_9 (.D(R2D), .en(WE2), .Q(R2), .clk(clk), .clr(reset));
  Register #(.width(32)) register_10 (.D(R10D), .en(WE10), .Q(R10), .clk(clk), .clr(reset));
  Register #(.width(32)) register_11 (.D(R18D), .en(WE18), .Q(R18), .clk(clk), .clr(reset));
  Register #(.width(32)) register_12 (.D(R26D), .en(WE26), .Q(R26), .clk(clk), .clr(reset));
  Register #(.width(32)) register_13 (.D(R3D), .en(WE3), .Q(R3), .clk(clk), .clr(reset));
  Register #(.width(32)) register_14 (.D(R11D), .en(WE11), .Q(R11), .clk(clk), .clr(reset));
  Register #(.width(32)) register_15 (.D(R19D), .en(WE19), .Q(R19), .clk(clk), .clr(reset));
  Register #(.width(32)) register_16 (.D(R27D), .en(WE27), .Q(R27), .clk(clk), .clr(reset));
  Register #(.width(32)) register_17 (.D(R4D), .en(WE4), .Q(R4), .clk(clk), .clr(reset));
  Register #(.width(32)) register_18 (.D(R12D), .en(WE12), .Q(R12), .clk(clk), .clr(reset));
  Register #(.width(32)) register_19 (.D(R20D), .en(WE20), .Q(R20), .clk(clk), .clr(reset));
  Register #(.width(32)) register_20 (.D(R28D), .en(WE28), .Q(R28), .clk(clk), .clr(reset));
  Register #(.width(32)) register_21 (.D(R5D), .en(WE5), .Q(R5), .clk(clk), .clr(reset));
  Register #(.width(32)) register_22 (.D(R13D), .en(WE13), .Q(R13), .clk(clk), .clr(reset));
  Register #(.width(32)) register_23 (.D(R21D), .en(WE21), .Q(R21), .clk(clk), .clr(reset));
  Register #(.width(32)) register_24 (.D(R29D), .en(WE29), .Q(R29), .clk(clk), .clr(reset));
  Register #(.width(32)) register_25 (.D(R6D), .en(WE6), .Q(R6), .clk(clk), .clr(reset));
  Register #(.width(32)) register_26 (.D(R14D), .en(WE14), .Q(R14), .clk(clk), .clr(reset));
  Register #(.width(32)) register_27 (.D(R22D), .en(WE22), .Q(R22), .clk(clk), .clr(reset));
  Register #(.width(32)) register_28 (.D(R30D), .en(WE30), .Q(R30), .clk(clk), .clr(reset));
  Multiplexer #(.select(5), .width(32)) multiplexer_1 (
    .in0(R0), .in1(R1), .in2(R2), .in3(R3), .in4(R4), .in5(R5), .in6(R6), .in7(R7), .in8(R8), .in9(R9),
    .in10(R10), .in11(R11), .in12(R12), .in13(R13), .in14(R14), .in15(R15), .in16(R16), .in17(R17),
    .in18(R18), .in19(R19), .in20(R20), .in21(R21), .in22(R22), .in23(R23), .in24(R24), .in25(R25),
    .in26(R26), .in27(R27), .in28(R28), .in29(R29), .in30(R30), .in31(R31), .out(RD1), .sel(A1));  // open: en
  Register #(.width(32)) register_29 (.D(R7D), .en(WE7), .Q(R7), .clk(clk), .clr(reset));
  Register #(.width(32)) register_30 (.D(R15D), .en(WE15), .Q(R15), .clk(clk), .clr(reset));
  Register #(.width(32)) register_31 (.D(R23D), .en(WE23), .Q(R23), .clk(clk), .clr(reset));
  Register #(.width(32)) register_32 (.D(R31D), .en(WE31), .Q(R31), .clk(clk), .clr(reset));
  Multiplexer #(.select(5), .width(32)) multiplexer_2 (
    .in0(R0), .in1(R1), .in2(R2), .in3(R3), .in4(R4), .in5(R5), .in6(R6), .in7(R7), .in8(R8), .in9(R9),
    .in10(R10), .in11(R11), .in12(R12), .in13(R13), .in14(R14), .in15(R15), .in16(R16), .in17(R17),
    .in18(R18), .in19(R19), .in20(R20), .in21(R21), .in22(R22), .in23(R23), .in24(R24), .in25(R25),
    .in26(R26), .in27(R27), .in28(R28), .in29(R29), .in30(R30), .in31(R31), .out(RD2), .sel(A2));  // open: en
endmodule
