// Logisim project IM.circ as structural Verilog: 1 circuit, main circuit IM
module IM (
  input  [31:0] Address,
  output [31:0] instruction
);

  ROM #(.addrWidth(5), .dataWidth(32)) rom_1 (.addr(Address[6:2]), .data(instruction));  // open: sel
endmodule
