// Logisim project NPC.circ as structural Verilog: 1 circuit, main circuit NPC
module NPC (
  input  in_1,
  input  [31:0] PC,
  input  [15:0] immediate,
  output [31:0] nextPC
);

  wire [31:0] adder_1_out, adder_2_out, bit_extender_1_out, shifter_1_out;

  Adder #(.width(32)) adder_1 (.a(PC), .b(32'h4), .out(adder_1_out));  // open: cin, cout
  assign bit_extender_1_out = {{16{immediate[15]}}, immediate};  // Bit_Extender bit_extender_1
  Shifter #(.width(32)) shifter_1 (.in(bit_extender_1_out), .\dist (5'b00010), .out(shifter_1_out));
  Adder #(.width(32)) adder_2 (.a(adder_1_out), .b(shifter_1_out), .out(adder_2_out));  // open: cin, cout
  Multiplexer #(.width(32)) multiplexer_1 (.in0(adder_1_out), .in1(adder_2_out), .out(nextPC), .sel(in_1));  // open: en
endmodule
